# Fritzing sketch bluetooth (saved by Fritzing 0.9.3b)
breadboards: 1

parts:
  Componente1 = Arduino BT
  J1 = Basic Servo
  Componente2 = Bluetooth HC-05 Macho

nets:
  GND: Componente1.GND, J1.gnd, Componente2.GND
  N1: Componente1.PWM_D9, J1.pulse
  N2: Componente1.D2, Componente2.RXD
  N3: Componente1.PWM_D3, Componente2.TXD
  VCC: Componente1.5V, J1.vcc, Componente2.VCC
